# Fritzing sketch datalogger (saved by Fritzing 0.9.2b)

parts:
  Part1 = Arduino Uno (Rev3) - ICSP  # not connected
  Part2 = Memoire 1.0 - SD card log shield
  Part3 = BH1750
  DHT1 = DHT22 Humidity and Temperature Sensor

nets:
  N1: Part2.DIG_5, DHT1.DATA
  N2: Part2.A_IN_4, Part3.SCL
  N3: Part2.A_IN_5, Part3.SDA

custom parts:
  BH1750: Light Sensor
